# Fritzing sketch ESP32_Button_bb (saved by Fritzing 0.9.8b)
breadboards: 1

parts:
  S1 = Pushbutton [package="[THT]"]
  R1 = Resistor [tolerance=±5% resistance=10k package="2010 [SMD]"]
  Part1 = Adafruit HUZZAH32 ESP32 Feather [part_number="Adafruit #3405"]

nets:
  N1: S1.Pin_1, S1.Pin_2, R1.Pin_0, Part1.A2_I34
  N2: S1.Pin_3, S1.Pin_4, Part1.3.3V
  N3: R1.Pin_1, Part1.GND
