# Fritzing sketch NanoIot_Button (saved by Fritzing 0.9.8b)
breadboards: 1

parts:
  S1 = Pushbutton [package="[THT]"]
  R1 = Resistor [tolerance=±5% resistance=10k package="2010 [SMD]"]
  Part1 = Arduino Nano 33 IOT

nets (from the breadboard view):
  N1: S1.Pin_1, S1.Pin_2, R1.Pin_0, Part1.D2
  N2: S1.Pin_3, S1.Pin_4, Part1.3V3
  N3: R1.Pin_1, Part1.GND, Part1.D13~
  N4: Part1.RESET, Part1.A7
  N5: Part1.D11/MOSI, Part1.+5V

custom parts:
  Arduino Nano 33 IOT: The Arduino Nano 33 IoT is the easiest and cheapest point of entry to enhance existing devices (and creating new ones) to be part of the IoT and designing pico-network applications. Whether you are looking at building a sensor network connected to your office or home router, or if you want to create a BLE device sending data to a cellphone, the Nano 33 IoT is your one-stop-solution for many of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
